# Fritzing sketch scheme (saved by Fritzing 1.0.5)
breadboards: 1

parts:
  Компонент1 = Arduino Uno (Rev3) - ICSP
  J1 = Basic Servo
  HC-SR04_Sensor_1 = HC-SR04 Ultrasonic Distance Sensor
  RHT1 = Humidity and Temperature Sensor RHT03
  R1 = PHOTOCELL [package=photocell]
  R2 = Resistor [tolerance=±5% power=0.25W resistance=220 package=THT]

nets:
  N1: Компонент1.A0, R1.P$2, R2.Pin_0
  VCC: Компонент1.5V, J1.vcc, HC-SR04_Sensor_1.VCC, RHT1.Vcc, R1.P$1
  GND: Компонент1.GND, J1.gnd, HC-SR04_Sensor_1.GND, RHT1.GND_2, R2.Pin_1
  N2: Компонент1.D9_PWM, J1.pulse
  N3: Компонент1.D2, RHT1.Data-signal
  N4: Компонент1.D6_PWM, HC-SR04_Sensor_1.ECHO
  N5: Компонент1.D7, HC-SR04_Sensor_1.TRIG
